# Fritzing sketch Electronic Schematic RevB (saved by Fritzing 0.9.2b)
circuit board: 2.3cm x 2.3cm
circuit board: 2.3cm x 2.3cm
circuit board: 6.5cm x 4.5cm
circuit board: 2.3cm x 2.3cm
circuit board: 4.5cm x 4.5cm
breadboards: 7

parts:
  VCC2 = Battery block 9V
  R25 = Resistor [tolerance=±5% resistance=1k package=THT]
  M2 = DC Motor
  R28 = Resistor [tolerance=±5% resistance=10 package=THT]
  R29 = Resistor [tolerance=±5% resistance=1k package=THT]
  LED9 = LED - 5mm [color="Infrared (880nm)" package="5 mm [THT]"]
  R30 = Resistor [tolerance=±5% resistance=100 package=THT]
  R31 = Resistor [tolerance=±5% resistance=100 package=THT]
  J2 = Piezo Speaker
  R33 = Resistor [tolerance=±5% resistance=1k package=THT]
  S6 = Tilt Switch [package=THT]
  J3 = female pin header, 4 pins [form="♀ (female)"]
  J4 = female pin header, 6 pins [form="♀ (female)"]
  J5 = female pin header, 6 pins [form="♀ (female)"]
  R26 = Resistor [tolerance=±5% resistance=10 package=THT]
  R32 = Resistor [tolerance=±5% resistance=1k package=THT]
  Part2 = Arduino Nano (Rev3.0)
  S7 = Tilt Switch [package=THT]
  U2 = 7-SEGMENT-4DIGIT [package=7-segment-4digit-5641]
  R34 = Resistor [tolerance=±5% resistance=2.2k package=THT]
  BOTTOM = male pin header, 6 pins [form="♂ (male)"]
  R35 = Resistor [tolerance=±5% resistance=2.2k package=THT]
  R36 = Resistor [tolerance=±5% resistance=2.2k package=THT]
  R37 = Resistor [tolerance=±5% resistance=2.2k package=THT]
  R38 = Resistor [tolerance=±5% resistance=2.2k package=THT]
  TOP = male pin header, 6 pins [form="♂ (male)"]
  R39 = Resistor [tolerance=±5% resistance=2.2k package=THT]
  R40 = Resistor [tolerance=±5% resistance=2.2k package=THT]
  R41 = Resistor [tolerance=±5% resistance=2.2k package=THT]
  Q12 = NPN-Transistor [package="TO92 [THT]"]
  Q13 = NPN-Transistor [package="TO92 [THT]"]
  C1 = Electrolytic Capacitor [capacitance=10µF package="100 mil [THT, electrolytic]"]
  C2 = Electrolytic Capacitor [capacitance=10µF package="100 mil [THT, electrolytic]"]
  J6 = female pin header, 4 pins [form="♀ (female)"]
  J7 = female pin header, 4 pins [form="♀ (female)"]
  U3 = mystery part, 3 pins [chip_label="IR SEN"]
  LED10 = LED - 5mm [color="Red (633nm)" package="5 mm [THT]"]
  Q14 = NPN-Transistor [package="TO92 [THT]"]
  R42 = Resistor [tolerance=±5% resistance=1k package=THT]
  R43 = Resistor [tolerance=±5% resistance=1k package=THT]
  LED11 = LED - 5mm [color="Red (633nm)" package="5 mm [THT]"]
  U4 = mystery part, 3 pins [chip_label="IR SEN"]
  R44 = Resistor [tolerance=±5% resistance=1k package=THT]
  J8 = female pin header, 4 pins [form="♀ (female)"]
  J9 = female pin header, 4 pins [form="♀ (female)"]
  LED12 = LED - 5mm [color="Red (633nm)" package="5 mm [THT]"]
  U5 = mystery part, 3 pins [chip_label="IR SEN"]
  R45 = Resistor [tolerance=±5% resistance=1k package=THT]
  J10 = female pin header, 4 pins [form="♀ (female)"]
  J11 = female pin header, 4 pins [form="♀ (female)"]
  U1 = Voltage Regulator - 5V [package="TO220 [THT]"]
  R46 = Resistor [tolerance=±5% resistance=1k package=THT]
  R47 = Resistor [tolerance=±5% resistance=1k package=THT]

nets:
  GND: VCC2.-, J2.pin1, J3.pin4, Part2.GND, Q12.E, Q13.E, C1.-, C2.-, Q14.E, U1.GND, R46.Pin_1, R47.Pin_0
  N1: VCC2.+, Part2.VIN, C1.+, U1.input_voltage
  N2: R25.Pin_0, Part2.A5
  N3: R25.Pin_1, Q13.B
  N4: M2.pin_1, Q13.C
  N5: M2.pin_2, R26.Pin_0
  N6: R28.Pin_0, R33.Pin_0, J3.pin1, R26.Pin_1, R32.Pin_0, C2.+, U1.output_voltage
  N7: R28.Pin_1, LED9.anode
  N8: R29.Pin_0, Part2.D3
  N9: R29.Pin_1, Q12.B
  N10: LED9.cathode, Q12.C
  N11: R30.Pin_0, Part2.D11/MOSI
  N12: R30.Pin_1, R31.Pin_1, J2.pin2
  N13: R31.Pin_0, Part2.D12/MISO
  N14: R33.Pin_1, S7.Pin_2
  N15: S6.Pin_1, Part2.A7, R46.Pin_0
  N16: S6.Pin_2, R32.Pin_1
  N17: J3.pin2, Q14.C
  N18: J3.pin3, Part2.D2
  N19: J4.pin1, Part2.A4
  N20: J4.pin2, Part2.A3
  N21: J4.pin3, Part2.A2
  N22: J4.pin4, Part2.A1
  N23: J4.pin5, Part2.A0
  N24: J4.pin6, Part2.D13/SCK
  N25: J5.pin1, Part2.D10
  N26: J5.pin2, Part2.D9
  N27: J5.pin3, Part2.D8
  N28: J5.pin4, Part2.D7
  N29: J5.pin5, Part2.D6
  N30: J5.pin6, Part2.D5
  N31: Part2.D4, R42.Pin_1
  N32: Part2.A6, S7.Pin_1, R47.Pin_1
  N33: U2.DIG2, TOP.pin4
  N34: U2.DIG3, TOP.pin5
  N35: U2.DIG4, BOTTOM.pin6
  N36: U2.A, R41.Pin_0
  N37: U2.B, R39.Pin_0
  N38: U2.C, R37.Pin_0
  N39: U2.D, R35.Pin_0
  N40: U2.E, R34.Pin_0
  N41: U2.F, R40.Pin_0
  N42: U2.G, R38.Pin_0
  N43: U2.DP, R36.Pin_0
  N44: U2.DIG1, TOP.pin1
  N45: R34.Pin_1, BOTTOM.pin1
  N46: BOTTOM.pin2, R35.Pin_1
  N47: BOTTOM.pin3, R36.Pin_1
  N48: BOTTOM.pin4, R37.Pin_1
  N49: BOTTOM.pin5, R38.Pin_1
  N50: TOP.pin2, R41.Pin_1
  N51: TOP.pin3, R40.Pin_1
  N52: TOP.pin6, R39.Pin_1
  N53: J6.pin1, J7.pin1, U3.pin3, R43.Pin_1
  N54: J6.pin2, J7.pin2, LED10.cathode
  N55: J6.pin3, J7.pin3, U3.pin1
  N56: J6.pin4, J7.pin4, U3.pin2
  N57: LED10.anode, R43.Pin_0
  N58: Q14.B, R42.Pin_0
  N59: LED11.cathode, J8.pin2, J9.pin2
  N60: LED11.anode, R44.Pin_0
  N61: U4.pin1, J8.pin3, J9.pin3
  N62: U4.pin2, J8.pin4, J9.pin4
  N63: U4.pin3, R44.Pin_1, J8.pin1, J9.pin1
  N64: LED12.cathode, J10.pin2, J11.pin2
  N65: LED12.anode, R45.Pin_0
  N66: U5.pin1, J10.pin3, J11.pin3
  N67: U5.pin2, J10.pin4, J11.pin4
  N68: U5.pin3, R45.Pin_1, J10.pin1, J11.pin1

custom parts:
  7-SEGMENT-4DIGIT: if you need make parts, send me e-mail and write. Price 1 part=0.9 WMZ (http://www.wmtransfer.com/) ~ 0.9 Euro
